// Logisim project zhan_design.circ as structural Verilog: 10 circuits, main circuit main
module PC (
  input  [31:0] D,
  input  enable,
  input  clk,
  input  rst,
  output [31:0] pc_out
);

  Register #(.width(32)) register_1 (.D(D), .en(enable), .clk(clk), .Q(pc_out), .clr(rst));
endmodule

module Regx4 (
  input  [31:0] D,
  input  enable,
  input  clk,
  input  rst,
  output [31:0] reg_out
);

  Register #(.width(32)) register_1 (.D(D), .en(enable), .clk(clk), .Q(reg_out), .clr(rst));
endmodule

module main (
  input  rst
);

  wire clk_out, which_instruction_1_add, which_instruction_1_addi, which_instruction_1_jalr,
       which_instruction_1_lbu, which_instruction_1_lui, which_instruction_1_lw, which_instruction_1_sw,
       which_type_1_i_type, which_type_1_illegal, which_type_1_r_type, which_type_1_s_type,
       which_type_1_u_type;
  wire [4:0] my_decoder_1_rd, my_decoder_1_rs1, my_decoder_1_rs2;
  wire [6:0] my_decoder_1_opcode;
  wire [31:0] instruction_memory_1_instruction, pc_1_pc_out;

  Clock clk (.out(clk_out));
  PC pc_1 (.clk(clk_out), .rst(rst), .pc_out(pc_1_pc_out));  // open: D, enable
  instruction_memory instruction_memory_1 (.pc(pc_1_pc_out), .instruction(instruction_memory_1_instruction));
  my_decoder my_decoder_1 (
    .instruction(instruction_memory_1_instruction), .opcode(my_decoder_1_opcode), .rd(my_decoder_1_rd),
    .rs1(my_decoder_1_rs1), .rs2(my_decoder_1_rs2));  // open: funct3, funct7
  which_type which_type_1 (
    .opcode(my_decoder_1_opcode), .r_type(which_type_1_r_type), .i_type(which_type_1_i_type),
    .s_type(which_type_1_s_type), .u_type(which_type_1_u_type), .illegal(which_type_1_illegal));
  register_file register_file_1 (
    .rs1_addr(my_decoder_1_rs1), .rs2_addr(my_decoder_1_rs2), .rd_addr(my_decoder_1_rd), .clk(clk_out),
    .rst(rst));  // open: reg_write, rd_data, rs1_val, rs2_val
  immediate_generator immediate_generator_1 (
    .illegal(which_type_1_illegal), .i_type(which_type_1_i_type), .s_type(which_type_1_s_type),
    .instruction(instruction_memory_1_instruction), .u_type(which_type_1_u_type));  // open: imm
  which_instruction which_instruction_1 (
    .add(which_instruction_1_add), .addi(which_instruction_1_addi), .lui(which_instruction_1_lui),
    .lw(which_instruction_1_lw), .lbu(which_instruction_1_lbu), .sw(which_instruction_1_sw),
    .jalr(which_instruction_1_jalr));  // open: opcode, funct3, funct7, sb
  which_instruction which_instruction_2 (.opcode(my_decoder_1_opcode));  // open: funct3, funct7, add, addi, lui, lw, lbu, sw, sb, jalr
endmodule

module instruction_memory (
  input  [31:0] pc,
  output [31:0] instruction
);

  ROM #(.addrWidth(24), .dataWidth(32)) rom_1 (.addr(pc[25:2]), .data(instruction));
endmodule

module my_decoder (
  input  [31:0] instruction,
  output [6:0] opcode,
  output [4:0] rd,
  output [2:0] funct3,
  output [4:0] rs1,
  output [4:0] rs2,
  output [6:0] funct7
);


  assign funct3 = instruction[14:12];
  assign funct7 = instruction[31:25];
  assign opcode = instruction[6:0];
  assign rd = instruction[11:7];
  assign rs1 = instruction[19:15];
  assign rs2 = instruction[24:20];
endmodule

module which_type (
  input  [6:0] opcode,
  output r_type,
  output i_type,
  output s_type,
  output u_type,
  output illegal
);

  wire and_2_out, and_3_out, and_4_out;

  and and_1 (r_type, opcode[0], opcode[1], ~opcode[2], ~opcode[3], opcode[4], opcode[5], ~opcode[6]);  // AND_Gate
  and and_2 (and_2_out, opcode[0], opcode[1], ~opcode[2], ~opcode[3], opcode[4], ~opcode[5], ~opcode[6]);  // AND_Gate
  and and_3 (and_3_out, opcode[0], opcode[1], ~opcode[2], ~opcode[3], ~opcode[4], ~opcode[5], ~opcode[6]);  // AND_Gate
  and and_4 (and_4_out, opcode[0], opcode[1], opcode[2], ~opcode[3], ~opcode[4], opcode[5], opcode[6]);  // AND_Gate
  and and_5 (s_type, opcode[0], opcode[1], ~opcode[2], ~opcode[3], ~opcode[4], opcode[5], ~opcode[6]);  // AND_Gate
  and and_6 (u_type, opcode[0], opcode[1], opcode[2], ~opcode[3], opcode[4], opcode[5], ~opcode[6]);  // AND_Gate
  or or_1 (i_type, and_2_out, and_3_out, and_4_out);
  nor nor_1 (illegal, r_type, i_type, s_type, u_type);
endmodule

module alu (
  input  r_type,
  input  i_type,
  input  s_type,
  input  u_type,
  input  illegal,
  input  [31:0] instruction
);
endmodule

module register_file (
  input  [4:0] rs1_addr,
  input  [4:0] rs2_addr,
  input  [4:0] rd_addr,
  input  reg_write,
  input  [31:0] rd_data,
  input  clk,
  input  rst,
  output [31:0] rs1_val,
  output [31:0] rs2_val
);

  wire reg_0_out, reg_1_out, reg_2_out, reg_3_out, reg_4_out, reg_5_out, reg_6_out, reg_7_out, reg_8_out,
       reg_9_out, reg_10_out, reg_11_out, reg_12_out, reg_13_out, reg_14_out, reg_15_out;
  wire [31:0] regx4_1_reg_out, regx4_2_reg_out, regx4_3_reg_out, regx4_4_reg_out, regx4_5_reg_out,
       regx4_6_reg_out, regx4_7_reg_out, regx4_8_reg_out, regx4_9_reg_out, regx4_10_reg_out,
       regx4_11_reg_out, regx4_12_reg_out, regx4_13_reg_out, regx4_14_reg_out, regx4_15_reg_out,
       regx4_16_reg_out;

  and reg_0 (reg_0_out, ~rd_addr[0], ~rd_addr[1], ~rd_addr[2], ~rd_addr[3], reg_write);  // AND_Gate
  and reg_1 (reg_1_out, rd_addr[0], ~rd_addr[1], ~rd_addr[2], ~rd_addr[3], reg_write);  // AND_Gate
  and reg_2 (reg_2_out, ~rd_addr[0], rd_addr[1], ~rd_addr[2], ~rd_addr[3], reg_write);  // AND_Gate
  and reg_3 (reg_3_out, rd_addr[0], rd_addr[1], ~rd_addr[2], ~rd_addr[3], reg_write);  // AND_Gate
  and reg_4 (reg_4_out, ~rd_addr[0], ~rd_addr[1], rd_addr[2], ~rd_addr[3], reg_write);  // AND_Gate
  and reg_5 (reg_5_out, rd_addr[0], ~rd_addr[1], rd_addr[2], ~rd_addr[3], reg_write);  // AND_Gate
  and reg_6 (reg_6_out, ~rd_addr[0], rd_addr[1], rd_addr[2], ~rd_addr[3], reg_write);  // AND_Gate
  and reg_7 (reg_7_out, rd_addr[0], rd_addr[1], rd_addr[2], ~rd_addr[3], reg_write);  // AND_Gate
  and reg_8 (reg_8_out, ~rd_addr[0], ~rd_addr[1], ~rd_addr[2], rd_addr[3], reg_write);  // AND_Gate
  and reg_9 (reg_9_out, rd_addr[0], ~rd_addr[1], ~rd_addr[2], rd_addr[3], reg_write);  // AND_Gate
  and reg_10 (reg_10_out, ~rd_addr[0], rd_addr[1], ~rd_addr[2], rd_addr[3], reg_write);  // AND_Gate
  and reg_11 (reg_11_out, rd_addr[0], rd_addr[1], ~rd_addr[2], rd_addr[3], reg_write);  // AND_Gate
  and reg_12 (reg_12_out, ~rd_addr[0], ~rd_addr[1], rd_addr[2], rd_addr[3], reg_write);  // AND_Gate
  and reg_13 (reg_13_out, rd_addr[0], ~rd_addr[1], rd_addr[2], rd_addr[3], reg_write);  // AND_Gate
  and reg_14 (reg_14_out, ~rd_addr[0], rd_addr[1], rd_addr[2], rd_addr[3], reg_write);  // AND_Gate
  and reg_15 (reg_15_out, rd_addr[0], rd_addr[1], rd_addr[2], rd_addr[3], reg_write);
  Regx4 regx4_1 (.D({32{1'b0}}), .enable(reg_0_out), .clk(clk), .rst(rst), .reg_out(regx4_1_reg_out));
  Regx4 regx4_2 (.D(rd_data), .enable(reg_1_out), .clk(clk), .rst(rst), .reg_out(regx4_2_reg_out));
  Regx4 regx4_3 (.D(rd_data), .enable(reg_2_out), .clk(clk), .rst(rst), .reg_out(regx4_3_reg_out));
  Regx4 regx4_4 (.D(rd_data), .enable(reg_3_out), .clk(clk), .rst(rst), .reg_out(regx4_4_reg_out));
  Regx4 regx4_5 (.D(rd_data), .enable(reg_4_out), .clk(clk), .rst(rst), .reg_out(regx4_5_reg_out));
  Regx4 regx4_6 (.D(rd_data), .enable(reg_5_out), .clk(clk), .rst(rst), .reg_out(regx4_6_reg_out));
  Regx4 regx4_7 (.D(rd_data), .enable(reg_6_out), .clk(clk), .rst(rst), .reg_out(regx4_7_reg_out));
  Regx4 regx4_8 (.D(rd_data), .enable(reg_7_out), .clk(clk), .rst(rst), .reg_out(regx4_8_reg_out));
  Regx4 regx4_9 (.D(rd_data), .enable(reg_8_out), .clk(clk), .rst(rst), .reg_out(regx4_9_reg_out));
  Regx4 regx4_10 (.D(rd_data), .enable(reg_9_out), .clk(clk), .rst(rst), .reg_out(regx4_10_reg_out));
  Regx4 regx4_11 (.D(rd_data), .enable(reg_10_out), .clk(clk), .rst(rst), .reg_out(regx4_11_reg_out));
  Regx4 regx4_12 (.D(rd_data), .enable(reg_11_out), .clk(clk), .rst(rst), .reg_out(regx4_12_reg_out));
  Regx4 regx4_13 (.D(rd_data), .enable(reg_12_out), .clk(clk), .rst(rst), .reg_out(regx4_13_reg_out));
  Regx4 regx4_14 (.D(rd_data), .enable(reg_13_out), .clk(clk), .rst(rst), .reg_out(regx4_14_reg_out));
  Regx4 regx4_15 (.D(rd_data), .enable(reg_14_out), .clk(clk), .rst(rst), .reg_out(regx4_15_reg_out));
  Regx4 regx4_16 (.D(rd_data), .enable(reg_15_out), .clk(clk), .rst(rst), .reg_out(regx4_16_reg_out));
  Multiplexer #(.select(4), .width(32)) multiplexer_1 (
    .in0(regx4_1_reg_out), .in1(regx4_2_reg_out), .in2(regx4_3_reg_out), .in3(regx4_4_reg_out),
    .in4(regx4_5_reg_out), .in5(regx4_6_reg_out), .in6(regx4_7_reg_out), .in7(regx4_8_reg_out),
    .in8(regx4_9_reg_out), .in9(regx4_10_reg_out), .in10(regx4_11_reg_out), .in11(regx4_12_reg_out),
    .in12(regx4_13_reg_out), .in13(regx4_14_reg_out), .in14(regx4_15_reg_out), .in15(regx4_16_reg_out),
    .out(rs1_val), .sel(rs1_addr[3:0]));
  Multiplexer #(.select(4), .width(32)) multiplexer_2 (
    .in0(regx4_1_reg_out), .in1(regx4_2_reg_out), .in2(regx4_3_reg_out), .in3(regx4_4_reg_out),
    .in4(regx4_5_reg_out), .in5(regx4_6_reg_out), .in6(regx4_7_reg_out), .in7(regx4_8_reg_out),
    .in8(regx4_9_reg_out), .in9(regx4_10_reg_out), .in10(regx4_11_reg_out), .in11(regx4_12_reg_out),
    .in12(regx4_13_reg_out), .in13(regx4_14_reg_out), .in14(regx4_15_reg_out), .in15(regx4_16_reg_out),
    .out(rs2_val), .sel(rs2_addr[3:0]));
endmodule

module immediate_generator (
  input  illegal,
  input  i_type,
  input  s_type,
  input  [31:0] instruction,
  input  u_type,
  output [31:0] imm
);

  wire [1:0] or_1_out;

  or or_1 (or_1_out[0], illegal, u_type);
  or or_2 (or_1_out[1], illegal, s_type);
  Multiplexer #(.select(2), .width(32)) multiplexer_1 (
    .in0({{21{instruction[31]}}, instruction[30:20]}),
    .in1({{21{instruction[31]}}, instruction[30:25], instruction[11:7]}),
    .in2({instruction[31:12], {12{1'b0}}}), .in3({32{1'b0}}), .out(imm), .sel(or_1_out));
endmodule

module which_instruction (
  input  [6:0] opcode,
  input  [2:0] funct3,
  input  [6:0] funct7,
  output add,
  output addi,
  output lui,
  output lw,
  output lbu,
  output sw,
  output sb,
  output jalr
);

  wire comparator_1_eq, comparator_2_eq, comparator_3_eq, comparator_4_eq, comparator_6_eq, comparator_7_eq,
       comparator_8_eq, comparator_9_eq, comparator_10_eq;

  Comparator #(.width(7)) comparator_1 (.a(opcode), .b(7'b0110011), .eq(comparator_1_eq));  // open: gt, lt
  Comparator #(.width(7)) comparator_2 (.a(opcode), .b(7'b0010011), .eq(comparator_2_eq));  // open: gt, lt
  Comparator #(.width(7)) comparator_3 (.a(opcode), .b(7'b0000011), .eq(comparator_3_eq));  // open: gt, lt
  Comparator #(.width(7)) comparator_4 (.a(opcode), .b(7'b0100011), .eq(comparator_4_eq));  // open: gt, lt
  Comparator #(.width(7)) comparator_5 (.a(opcode), .b(7'b0110111), .eq(lui));  // open: gt, lt
  Comparator #(.width(7)) comparator_6 (.a(opcode), .b(7'b1100111), .eq(comparator_6_eq));  // open: gt, lt
  Comparator #(.width(3)) comparator_7 (.a(funct3), .b(3'b000), .eq(comparator_7_eq));  // open: gt, lt
  Comparator #(.width(3)) comparator_8 (.a(funct3), .b(3'b010), .eq(comparator_8_eq));  // open: gt, lt
  Comparator #(.width(3)) comparator_9 (.a(funct3), .b(3'b100), .eq(comparator_9_eq));  // open: gt, lt
  Comparator #(.width(7)) comparator_10 (.a(funct7), .b({7{1'b0}}), .eq(comparator_10_eq));  // open: gt, lt
  and and_1 (add, comparator_1_eq, comparator_7_eq, comparator_10_eq);
  and and_2 (addi, comparator_2_eq, comparator_7_eq);
  and and_3 (lw, comparator_3_eq, comparator_8_eq);
  and and_4 (lbu, comparator_3_eq, comparator_9_eq);
  and and_5 (sw, comparator_4_eq, comparator_8_eq);
  and and_6 (sb, comparator_7_eq, comparator_4_eq);
  and and_7 (jalr, comparator_6_eq, comparator_7_eq);
endmodule
